# Fritzing sketch AS3340_Test (saved by Fritzing 0.9.4)
breadboards: 1

parts:
  IC1 = IC, DIP package, 16 pins [chip_label=AS3340]
  R1 = Resistor [tolerance=±5% resistance=100k package=THT]
  R3 = Resistor [tolerance=±5% resistance=470 package=THT]
  R4 = Rotary Potentiometer (Small) [maximum_resistance=100kΩ package=THT]
  C1 = Film/Foil Capacitor [capacitance=100nF voltage=35V package="5mm [THT, pp]"]
  R5 = Resistor [tolerance=±5% resistance=100k package=THT]
  R6 = Resistor [tolerance=±5% resistance=1.8k package=THT]
  R7 = Resistor [tolerance=±5% resistance=1M package=THT]
  C2 = Film/Foil Capacitor [capacitance=100nF voltage=35V package="5mm [THT, pp]"]
  R8 = Resistor [tolerance=±5% resistance=470 package=THT]
  C3 = Film/Foil Capacitor [capacitance=100nF voltage=35V package="5mm [THT, pp]"]
  R9 = Resistor [tolerance=±5% resistance=27k package=THT]
  R10 = TRIMPOT [package=trimpot_pth_s3_lock]
  R11 = Resistor [tolerance=±5% resistance=680 package=THT]
  R12 = Resistor [tolerance=±5% resistance=5.6k package=THT]
  R13 = Resistor [tolerance=±5% resistance=5.6k package=THT]
  C4 = Ceramic Capacitor [capacitance=100nF package="100 mil [THT, multilayer]"]
  C5 = Electrolytic Capacitor [capacitance=1µF package="100 mil [THT, electrolytic]"]
  C6 = Electrolytic Capacitor [capacitance=1µF package="100 mil [THT, electrolytic]"]

nets:
  N1: IC1.pin1, R9.Pin_1
  N2: IC1.pin2, R12.Pin_1
  N3: IC1.pin3, R10.CCW, R10.WIPER, R11.Pin_0, R12.Pin_0
  N4: IC1.pin4, R13.Pin_0
  N5: IC1.pin11, C2.+
  N6: IC1.pin12, C1.+, R6.Pin_0, C2.-, C3.-, R13.Pin_1, C4.1, C5.-, C6.+
  N7: IC1.pin13, R7.Pin_1, R8.Pin_0
  N8: IC1.pin14, R6.Pin_1
  N9: IC1.pin15, R1.Pin_1, R3.Pin_1, R5.Pin_1
  N10: IC1.pin16, R4.leg2, R7.Pin_0, C4.0, C5.+
  N11: R1.Pin_0, R4.leg1, R4.wiper
  N12: R3.Pin_0, C1.-
  N13: R8.Pin_1, C3.+
  N14: R9.Pin_0, R10.CW
  N15: R11.Pin_1, C6.-

notes:
  CV
  Triangle
  Pulse
  Saw
  GND
  +12V
  -12V
  GND
  PWM
  AS3340
  1 Scale1 16 VCC
  2 Scale2 15 VFCI
  3 VEE 14 Scale
  4 VP 13 VLFI
  5 VPWM 12 GND
  6 VHSI 11 Cap
  7 VHFT 10 VTO
  8 VSO 9 VSSI
